# Fritzing sketch Watch'Int (saved by Fritzing 0.9.2b)
breadboards: 1

parts:
  Part1 = Bluetooth HC-05 Macho
  Part2 = Arduino Uno (Rev3)
  Grove1 = Grove OLED 128x96
  SG2 = Buzzer 12mm [package=buzzer-12mm-ns]
  S1 = SWITCH-MOMENTARY-2 [package=tactile_switch_tall]  # not connected
  R1 = Resistor [tolerance=±5% resistance=220 package=THT]

nets:
  N1: Part1.TXD, Part2.D10_PWM/SS
  N2: Part1.RXD, Part2.D11_PWM/MOSI
  VCC: Part1.VCC, Part2.5V, Grove1.VCC, SG2.1
  GND: Part1.GND, Part2.GND, Grove1.GND, R1.Pin_1
  N3: Part2.A4/SDA, Grove1.SDA
  N4: Part2.A5/SCL, Grove1.SCL
  N5: Part2.D9_PWM, SG2.2
  N6: Part2.D7, R1.Pin_0
